// Logisim project BullsAndCows.circ as structural Verilog: 1 circuit, main circuit main
module main (
);

  wire _0_out, _1_out, _2_out, _3_out, _4_out, _5_out, _6_out, _7_out, _8_out, _9_out, button_2_out,
       button_out, Clock, dead, decoder_1_out0, decoder_1_out1, decoder_1_out2, decoder_1_out3, enter, match,
       same_digit_1_same_digit;
  wire [1:0] digit_selector_digit_place;
  wire [2:0] state, wins_lives_memory_lives;
  wire [3:0] bit_extender_1_out, bulls_1_bulls, cows_1_cows, D0, D1, D2, D3, I0, I1, I2, I3, S0, S1, S2, S3,
       T0, T1, T2, T3, wins_lives_memory_wins;

  Clock clock_1 (.out(Clock));
  Button _2 (.out(_2_out));
  Button _1 (.out(_1_out));
  Button _5 (.out(_5_out));
  Button _4 (.out(_4_out));
  Button _8 (.out(_8_out));
  Button _7 (.out(_7_out));
  Button _0 (.out(_0_out));
  Button button (.out(button_out));
  Button u_Enter (.out(enter));
  Button _3 (.out(_3_out));
  Button _6 (.out(_6_out));
  Button _9 (.out(_9_out));
  Button button_2 (.out(button_2_out));
  digit_selector digit_selector (
    .L(button_out), .R(button_2_out), .clock(Clock), .state(state), .Digit_Place(digit_selector_digit_place));
  digit_input number_input (
    ._0(_0_out), ._1(_1_out), ._2(_2_out), ._3(_3_out), ._4(_4_out), ._5(_5_out), ._6(_6_out), ._7(_7_out),
    ._8(_8_out), ._9(_9_out), .clock(Clock), .in_12(digit_selector_digit_place), .State(state), .I0(I0),
    .I1(I1), .I2(I2), .I3(I3));
  Hex_Digit_Display hex_digit_display_1 (.value(wins_lives_memory_wins));  // open: dp
  wins_lives_memory wins_lives_memory (
    .match(match), .state(state), .clock(Clock), .wins(wins_lives_memory_wins),
    .lives(wins_lives_memory_lives));
  Hex_Digit_Display hex_digit_display_2 (.value(bit_extender_1_out));  // open: dp
  assign bit_extender_1_out = {{1{1'b0}}, wins_lives_memory_lives};  // Bit_Extender bit_extender_1
  and and_1 (dead, wins_lives_memory_lives[0], ~wins_lives_memory_lives[1], ~wins_lives_memory_lives[2]);  // AND_Gate
  store_memory setup_digits (
    .I0(I0), .I1(I1), .I2(I2), .I3(I3), .Enter(enter), .state(state), .clock(Clock), .s0(S0), .s1(S1),
    .s2(S2), .s3(S3));
  try_memory test_digits (
    .I0(I0), .I1(I1), .I2(I2), .I3(I3), .Enter(enter), .state(state), .clock(Clock), .tr0(T0), .tr1(T1),
    .tr2(T2), .tr3(T3));
  // Probe on state
  mik_state_controller state_control (.dead(dead), .win(match), .enter(enter), .Clock(Clock), .state(state));
  Decoder #(.select(2)) decoder_1 (
    .out0(decoder_1_out0), .out1(decoder_1_out1), .out2(decoder_1_out2), .out3(decoder_1_out3),
    .sel(digit_selector_digit_place));  // open: en
  LED led_1 (.in(decoder_1_out3));
  Hex_Digit_Display hex_digit_display_3 (.value(D3));  // open: dp
  same_digit same_digit_1 (.t1(T0), .t2(T1), .t3(T2), .t4(T3), .same_digit(same_digit_1_same_digit));
  bulls bulls_1 (.Bulls(bulls_1_bulls));  // open: tr1, tr2, tr3, tr4, sr1, sr2, sr3, sr4, out_10
  cows cows_1 (.Cows(cows_1_cows));  // open: tr1, tr2, tr3, tr4, sr1, sr2, sr3, sr4
  LED led_2 (.in(decoder_1_out1));
  LED led_3 (.in(decoder_1_out2));
  Hex_Digit_Display hex_digit_display_4 (.value(D1));  // open: dp
  Hex_Digit_Display hex_digit_display_5 (.value(D2));  // open: dp
  LED led_4 (.in(decoder_1_out0));
  Hex_Digit_Display hex_digit_display_6 (.value(D0));  // open: dp
  digit_display digit_display_picker (
    .I0(I0), .I1(I1), .I2(I2), .I3(I3), .S0(S0), .S1(S1), .S2(S2), .S3(S3), .state(state), .D0(D0), .D1(D1),
    .D2(D2), .D3(D3));
  Hex_Digit_Display hex_digit_display_7 (.value(cows_1_cows));  // open: dp
  Hex_Digit_Display hex_digit_display_8 (.value(bulls_1_bulls));  // open: dp
  Hex_Digit_Display hex_digit_display_9 (.value(S2));  // open: dp
  Hex_Digit_Display hex_digit_display_10 (.value(S3));  // open: dp
  Hex_Digit_Display hex_digit_display_11 (.value(S1));  // open: dp
  Hex_Digit_Display hex_digit_display_12 (.value(S0));  // open: dp

  // Notes on the sheet:
  //   Inputs
  //   Wins
  //   Lives
  //   Input DisplayDigits
  //   Bulls
  //   Saved Setup Digits
  //   Cows
endmodule
